// Logisim project Assignment 11.circ as structural Verilog: 1 circuit, main circuit main
module main (
  input  A,
  input  B,
  output F__A___B,
  output F__A___B_2,
  output F__A___B_3
);

  wire and_1_out, and_2_out, not_1_out, not_2_out;

  not not_1 (not_1_out, A);
  not not_2 (not_2_out, B);
  and and_1 (and_1_out, not_2_out, not_1_out);
  and and_2 (and_2_out, B, A);
  and and_3 (F__A___B_2, A, not_2_out);
  and and_4 (F__A___B_3, not_1_out, B);
  or or_1 (F__A___B, and_1_out, and_2_out);

  // Notes on the sheet:
  //   Assignment - 11
  //   1 Bit Comparator
  //   Name - Debarghaya Mitra        Enrollment Number - 12024052002215        Branch - CSE        Section - C        Roll No - 248
endmodule
