// Logisim project Assignment 12.circ as structural Verilog: 1 circuit, main circuit main
module main (
  input  A0,
  input  A1,
  input  B0,
  input  B1,
  output F__A___B,
  output F__A___B_2,
  output F__A___B_3
);

  wire and_2_out, and_3_out, and_4_out, and_5_out, not_1_out, not_2_out, not_3_out, not_4_out, xnor_1_out,
       xnor_2_out;

  not not_1 (not_1_out, A0);
  not not_2 (not_2_out, B0);
  not not_3 (not_3_out, A1);
  not not_4 (not_4_out, B1);
  xnor xnor_1 (xnor_1_out, A1, B1);
  xnor xnor_2 (xnor_2_out, A0, B0);
  and and_1 (F__A___B, xnor_1_out, xnor_2_out);
  and and_2 (and_2_out, A1, not_4_out);
  and and_3 (and_3_out, A0, xnor_1_out, not_2_out);
  and and_4 (and_4_out, not_3_out, B1);
  and and_5 (and_5_out, not_1_out, xnor_1_out, B0);
  or or_1 (F__A___B_2, and_2_out, and_3_out);
  or or_2 (F__A___B_3, and_4_out, and_5_out);

  // Notes on the sheet:
  //   Name - Debarghaya Mitra        Enrollment Number - 12024052002215        Branch - CSE        Section - C        Roll No - 248
  //   Assignment - 12
  //   2 Bit Comparator
endmodule
