// Logisim project Assignment 3.circ as structural Verilog: 1 circuit, main circuit main
module main (
  input  A,
  input  B,
  input  C,
  input  D,
  output F___A_prime_B___C_prime_D
);

  wire and_1_out, and_2_out, not_1_out, not_2_out;

  not not_1 (not_1_out, A);
  not not_2 (not_2_out, C);
  and and_1 (and_1_out, not_1_out, B);
  and and_2 (and_2_out, not_2_out, D);
  or or_1 (F___A_prime_B___C_prime_D, and_1_out, and_2_out);

  // Notes on the sheet:
  //   A'
  //   C'
  //   Assignment - 3
  //   Name - Debarghaya Mitra        Enrollment Number - 12024052002215        Branch - CSE        Section - C        Roll No - 248
  //   A'B
  //   C'D
endmodule
